// Logisim project 4to1Multiplexer.circ as structural Verilog: 1 circuit, main circuit 4to1Multiplexer
module _4to1Multiplexer (
  input  [7:0] _0,
  input  [7:0] _1,
  input  [7:0] _2,
  input  [7:0] nused,
  input  [1:0] in_5,
  output [7:0] out_6
);

  wire [7:0] multiplexer_1_out, multiplexer_2_out;

  Multiplexer #(.width(8), .enable("false")) multiplexer_1 (.in0(_0), .in1(_1), .out(multiplexer_1_out), .sel(in_5[0]));
  Multiplexer #(.width(8), .enable("false")) multiplexer_2 (
    .in0(_2), .in1(nused), .out(multiplexer_2_out), .sel(in_5[0]));
  Multiplexer #(.width(8), .enable("false")) multiplexer_3 (
    .in0(multiplexer_1_out), .in1(multiplexer_2_out), .out(out_6), .sel(in_5[1]));
endmodule
