// Logisim project bumpIncoder8.circ as structural Verilog: 1 circuit, main circuit bumpIncoder8
module bumpIncoder8 (
  input  [7:0] start_data,
  input  start,
  input  clock,
  input  reset,
  output [7:0] display1,
  output [7:0] display3,
  output [7:0] display5,
  output [7:0] display7,
  output [7:0] display2,
  output [7:0] display4,
  output [7:0] display6,
  output [7:0] display8,
  output [7:0] final_data,
  output start_output,
  output clock_output,
  output reset_output
);

  Register register_1 (.D(start_data), .en(start), .Q(display1), .clk(clock), .clr(reset));
  Register register_2 (.D(display1), .en(start), .Q(display2), .clk(clock), .clr(reset));
  Register register_3 (.D(display2), .en(start), .Q(display3), .clk(clock), .clr(reset));
  Register register_4 (.D(display4), .en(start), .Q(display5), .clk(clock), .clr(reset));
  Register register_5 (.D(display3), .en(start), .Q(display4), .clk(clock), .clr(reset));
  Register register_6 (.D(display5), .en(start), .Q(display6), .clk(clock), .clr(reset));
  Register register_7 (.D(display6), .en(start), .Q(display7), .clk(clock), .clr(reset));
  Register register_8 (.D(display7), .en(start), .Q(display8), .clk(clock), .clr(reset));

  assign clock_output = clock;
  assign final_data = display8;
  assign reset_output = reset;
  assign start_output = start;
endmodule
