// Logisim project character32.circ as structural Verilog: 1 circuit, main circuit character32
module character32 (
  input  [3:0] \index_4개씩1세트 ,
  input  start,
  output [31:0] \output 
);

  ROM #(.addrWidth(4), .dataWidth(32)) rom_1 (.addr(\index_4개씩1세트 ), .data(\output ), .sel(start));

  // Notes on the sheet:
  //   contents of rom_1 (hex, n*v repeats v):
  //   37 1e 16 3f 27 1e 16 2f 37 1e 16 2f
endmodule
