// Logisim project ground.circ as structural Verilog: 1 circuit, main circuit main
module main (
  input  [7:0] \input ,
  input  start,
  input  clock,
  input  reset,
  output [7:0] out_5,
  output [7:0] out_6,
  output [7:0] out_7,
  output [7:0] out_8,
  output [7:0] out_9,
  output [7:0] out_10,
  output [7:0] out_11,
  output [7:0] out_12
);

  Register register_1 (.D(\input ), .en(start), .Q(out_7), .clk(clock), .clr(reset));
  Register register_2 (.D(out_7), .en(start), .Q(out_8), .clk(clock), .clr(reset));
  Register register_3 (.D(out_8), .en(start), .Q(out_9), .clk(clock), .clr(reset));
  Register register_4 (.D(out_9), .Q(out_10), .clk(clock), .clr(reset));  // open: en
  Register register_5 (.D(out_10), .en(start), .Q(out_5), .clk(clock), .clr(reset));
  Register register_6 (.D(out_5), .en(start), .Q(out_11), .clk(clock), .clr(reset));
  Register register_7 (.D(out_11), .en(start), .Q(out_6), .clk(clock), .clr(reset));
  Register register_8 (.D(out_6), .en(start), .Q(out_12), .clk(clock), .clr(reset));
endmodule
