// Logisim project jump.circ as structural Verilog: 1 circuit, main circuit doubleJump
module doubleJump (
  input  [7:0] i1,
  input  [7:0] i2,
  input  [7:0] i3,
  input  [7:0] i4,
  input  [1:0] jump,
  input  enable,
  input  clock,
  input  reset,
  output [7:0] out_9
);

  wire undriven;
  wire [7:0] n4to1multiplexer_1_out_6;

  _4to1Multiplexer u_4to1multiplexer_1 (
    ._0(i1), ._1(i2), ._2(i3), .nused(i4), .in_5(jump), .out_6(n4to1multiplexer_1_out_6));
  Register register_1 (.D(n4to1multiplexer_1_out_6), .en(undriven), .Q(out_9), .clk(clock), .clr(reset));
endmodule
