// Logisim project jump32.circ as structural Verilog: 1 circuit, main circuit jump32
module jump32 (
  input  [31:0] character1,
  input  [31:0] character2,
  input  [31:0] character3,
  input  [31:0] character4,
  input  isJump,
  output [31:0] out_6,
  output [31:0] out_7,
  output [31:0] out_8,
  output [31:0] out_9
);

  wire and_1_out, and_2_out, and_3_out, and_4_out, and_5_out, clock_1_out, counter_1_carry, d_ff_1_q,
       d_ff_2_q, d_ff_3_q, d_ff_4_q, d_ff_5_q, not_1_out, not_2_out, or_1_out;
  wire [2:0] counter_1_q;
  wire [4:0] multiplexer_1_out;

  Clock clock_1 (.out(clock_1_out));
  and and_1 (and_1_out, isJump, d_ff_2_q);
  and and_2 (and_2_out, isJump, d_ff_3_q);
  and and_3 (and_3_out, isJump, d_ff_4_q);
  and and_4 (and_4_out, isJump, d_ff_5_q);
  D_Flip_Flop d_ff_1 (.clk(clock_1_out), .D(and_1_out), .Q(d_ff_1_q));  // open: Qn, preset, en, reset
  D_Flip_Flop d_ff_2 (.clk(clock_1_out), .D(and_2_out), .Q(d_ff_2_q));  // open: Qn, preset, en, reset
  D_Flip_Flop d_ff_3 (.clk(clock_1_out), .D(and_3_out), .Q(d_ff_3_q));  // open: Qn, preset, en, reset
  D_Flip_Flop d_ff_4 (.clk(clock_1_out), .D(and_4_out), .Q(d_ff_4_q));  // open: Qn, preset, en, reset
  D_Flip_Flop d_ff_5 (.clk(clock_1_out), .D(isJump), .Q(d_ff_5_q));  // open: Qn, preset, en, reset
  not not_1 (not_1_out, isJump);
  or or_1 (or_1_out, not_1_out, d_ff_1_q);
  Counter #(.width(3), .max('h4)) counter_1 (
    .load(or_1_out), .Q(counter_1_q), .carry(counter_1_carry), .clk(and_5_out));  // open: D, count, clr
  and and_5 (and_5_out, clock_1_out, not_2_out);
  not not_2 (not_2_out, counter_1_carry);
  Multiplexer #(.select(3), .width(5)) multiplexer_1 (
    .in0({5{1'b0}}), .in1(5'b01000), .in2(5'b01100), .in3(5'b01110), .in4(5'b01110), .out(multiplexer_1_out),
    .sel(counter_1_q), .en(1'b1));  // open: in5, in6, in7
  Shifter #(.width(32)) shifter_1 (.in(character1), .\dist (multiplexer_1_out), .out(out_6));
  Shifter #(.width(32)) shifter_2 (.in(character2), .\dist (multiplexer_1_out), .out(out_7));
  Shifter #(.width(32)) shifter_3 (.in(character3), .\dist (multiplexer_1_out), .out(out_8));
  Shifter #(.width(32)) shifter_4 (.in(character4), .\dist (multiplexer_1_out), .out(out_9));

  // Notes on the sheet:
  //   character
  //   distance
  //   output_character
endmodule
