// Logisim project pushBump8.circ as structural Verilog: 1 circuit, main circuit pushBump8
module pushBump8 (
  input  [7:0] empty_block,
  input  [7:0] block2,
  input  [7:0] block1,
  input  start,
  input  clock,
  input  reset,
  input  making,
  output [7:0] \output 
);

  wire not_1_out;
  wire [7:0] controlled_buffer_1_out, controlled_buffer_2_out, controlled_buffer_4_out, register_1_q,
       register_2_q, register_3_q, register_5_q;

  not not_1 (not_1_out, making);
  Register register_1 (.D(empty_block), .en(start), .Q(register_1_q), .clk(clock), .clr(reset));
  assign controlled_buffer_1_out = not_1_out ? register_1_q : 8'bz;  // Controlled_Buffer controlled_buffer_1
  assign controlled_buffer_2_out = making ? block2 : 8'bz;  // Controlled_Buffer controlled_buffer_2
  Register register_2 (.D(controlled_buffer_1_out), .en(start), .Q(register_2_q), .clk(clock), .clr(reset));
  assign controlled_buffer_2_out = not_1_out ? register_2_q : 8'bz;  // Controlled_Buffer controlled_buffer_3
  assign controlled_buffer_4_out = making ? block1 : 8'bz;  // Controlled_Buffer controlled_buffer_4
  Register register_3 (.D(controlled_buffer_2_out), .en(start), .Q(register_3_q), .clk(clock), .clr(reset));
  assign controlled_buffer_4_out = not_1_out ? register_3_q : 8'bz;  // Controlled_Buffer controlled_buffer_5
  Register register_4 (.D(register_5_q), .en(start), .Q(\output ), .clk(clock), .clr(reset));
  Register register_5 (.D(controlled_buffer_4_out), .en(start), .Q(register_5_q), .clk(clock), .clr(reset));
endmodule
