// Logisim project test2.circ as structural Verilog: 1 circuit, main circuit main
module main (
  input  [31:0] in_1,
  input  [31:0] in_2,
  input  [31:0] in_3,
  input  [31:0] in_4,
  input  [31:0] in_5,
  input  [31:0] in_6,
  input  start,
  input  reset,
  input  isMake,
  input  [7:0] delayTime,
  input  start_2,
  input  start_3,
  output \output 
);

  wire bumpcounter_1_output, clock_2_out, clock_out, counter_1_carry, not_1_out, or_1_out, register_1_q,
       undriven_2;
  wire [7:0] undriven;
  wire [31:0] main_1_p11, main_2_display1, main_2_display2, main_2_display3, main_2_display4,
       main_2_display5, main_2_display6, main_2_display7, main_2_display8, main_2_display9, main_2_display10,
       main_2_display11, main_2_display12, main_2_display13, main_2_display14, main_2_display15,
       main_2_display16, main_2_display17, main_2_display18, main_2_display19, main_2_display20,
       main_2_display21, main_2_display22, main_2_display23, main_2_display24, main_2_display25,
       main_2_display26, main_2_display27, main_2_display28, main_2_display29, main_2_display30,
       main_2_display31, main_2_display32;

  Clock clock (.out(clock_out));
  or or_1 (or_1_out, isMake, bumpcounter_1_output);
  bumpCounter bumpcounter_1 (
    .delayTime(delayTime), .start(start_2), .clock(clock_2_out), .\output (bumpcounter_1_output));
  Clock clock_2 (.out(clock_2_out));
  // pushBump32_main main_1: pin names not known; wires that end beside it: start, clock_out, reset, or_1_out, in_1, in_2, in_3, in_4, in_5, in_6, main_1_p11
  DotMatrix #(.matrixcols(32), .matrixrows(32)) dotmatrix_1 (
    .col0(main_2_display1), .col1(main_2_display2), .col2(main_2_display3), .col3(main_2_display4),
    .col4(main_2_display5), .col5(main_2_display6), .col6(main_2_display7), .col7(main_2_display8),
    .col8(main_2_display9), .col9(main_2_display10), .col10(main_2_display11), .col11(main_2_display12),
    .col12(main_2_display13), .col13(main_2_display14), .col14(main_2_display15), .col15(main_2_display16),
    .col16(main_2_display17), .col17(main_2_display18), .col18(main_2_display19), .col19(main_2_display20),
    .col20(main_2_display21), .col21(main_2_display22), .col22(main_2_display23), .col23(main_2_display24),
    .col24(main_2_display25), .col25(main_2_display26), .col26(main_2_display27), .col27(main_2_display28),
    .col28(main_2_display29), .col29(main_2_display30), .col30(main_2_display31), .col31(main_2_display32));
  not not_1 (not_1_out, \output );
  Counter counter_1 (
    .load(start_3), .D(undriven), .count(not_1_out), .carry(counter_1_carry), .clk(undriven_2),
    .clr(register_1_q));  // open: Q
  bumpIncoder32_main main_2 (
    .start_data(main_1_p11), .start(start), .clock(clock_out), .reset(reset), .display1(main_2_display1),
    .display2(main_2_display2), .display3(main_2_display3), .display4(main_2_display4),
    .display5(main_2_display5), .display6(main_2_display6), .display7(main_2_display7),
    .display8(main_2_display8), .display9(main_2_display9), .display10(main_2_display10),
    .display11(main_2_display11), .display12(main_2_display12), .display13(main_2_display13),
    .display14(main_2_display14), .display15(main_2_display15), .display16(main_2_display16),
    .display17(main_2_display17), .display18(main_2_display18), .display19(main_2_display19),
    .display20(main_2_display20), .display21(main_2_display21), .display22(main_2_display22),
    .display23(main_2_display23), .display24(main_2_display24), .display25(main_2_display25),
    .display26(main_2_display26), .display27(main_2_display27), .display28(main_2_display28),
    .display29(main_2_display29), .display30(main_2_display30), .display31(main_2_display31),
    .display32(main_2_display32));  // open: final_data, start_output, clock_output, reset_output
  Register #(.width(1)) register_1 (
    .D(counter_1_carry), .en(start_3), .Q(register_1_q), .clk(undriven_2));  // open: clr
  Register #(.width(1)) register_2 (.D(register_1_q), .en(start_3), .Q(\output ), .clk(undriven_2));  // open: clr
endmodule
